# Fritzing sketch Space Invaders (saved by Fritzing 0.9.10b)
breadboards: 1

parts:
  S1 = Pushbutton [package="[THT]"]
  S2 = Pushbutton [package="[THT]"]
  S3 = Pushbutton [package="[THT]"]
  J1 = Piezo Speaker
  OLED_I2C1 = OLED 128x64 I2C Monochrome Display
  Part1 = Arduino Uno (Rev3)
  R2 = Resistor [tolerance=±5% power=0.25 resistance=220 package=THT]
  R3 = Resistor [tolerance=±5% power=0.25 resistance=220 package=THT]
  R4 = Resistor [tolerance=±5% power=0.25 resistance=220 package=THT]

nets:
  N1: S1.Pin_1, S1.Pin_2, R2.Pin_1
  N2: S1.Pin_3, S1.Pin_4, Part1.D2
  N3: S2.Pin_1, S2.Pin_2, R3.Pin_1
  N4: S2.Pin_3, S2.Pin_4
  N5: S3.Pin_1, S3.Pin_2, R4.Pin_1
  N6: S3.Pin_3, S3.Pin_4
  GND: J1.pin1, OLED_I2C1.GND, Part1.GND, R2.Pin_0, R3.Pin_0, R4.Pin_0
  N7: J1.pin2, Part1.D3_PWM
  N8: OLED_I2C1.SDA, Part1.A4/SDA
  N9: OLED_I2C1.SCK, Part1.A5/SCL
  VDD: OLED_I2C1.VDD, Part1.5V
